// Logisim project 10.2.circ as structural Verilog: 1 circuit, main circuit main
module main (
);

  wire and_1_out, and_2_out, and_3_out, and_4_out, clock_1_out, EM_2_q, EM_2_qn, EM_out, Flip_Between_q,
       Flip_Between_qn, L1_2_q, L1_2_qn, L1_out, L2_2_q, L2_2_qn, L2_out, or_1_out, or_2_out;

  Button L1 (.out(L1_out));
  Button EM (.out(EM_out));
  Button L2 (.out(L2_out));
  and and_1 (and_1_out, L1_out, EM_2_qn);
  and and_2 (and_2_out, L2_out, EM_2_qn);
  or or_1 (or_1_out, L2_out, EM_out);
  Clock #(.highDuration(5), .lowDuration(5)) clock_1 (.out(clock_1_out));
  or or_2 (or_2_out, and_1_out, EM_out);
  and and_3 (and_3_out, clock_1_out, ~EM_out, ~L1_out, ~L2_out);  // AND_Gate
  and and_4 (and_4_out, and_3_out, ~L1_out);  // AND_Gate
  D_Flip_Flop Flip_Between (
    .clk(and_4_out), .D(Flip_Between_qn), .Q(Flip_Between_q), .Qn(Flip_Between_qn), .preset(L2_out),
    .reset(L1_out));  // open: en
  D_Flip_Flop EM_2 (.clk(clock_1_out), .D(1'b0), .Q(EM_2_q), .Qn(EM_2_qn), .preset(EM_out));  // open: en, reset
  D_Flip_Flop L1_2 (
    .clk(clock_1_out), .D(Flip_Between_q), .Q(L1_2_q), .Qn(L1_2_qn), .preset(and_1_out), .reset(or_1_out));  // open: en
  D_Flip_Flop L2_2 (
    .clk(clock_1_out), .D(Flip_Between_qn), .Q(L2_2_q), .Qn(L2_2_qn), .preset(and_2_out), .reset(or_2_out));  // open: en
  LED EM_3 (.in(EM_2_qn));
  LED EM_4 (.in(EM_2_q));
  LED L1_3 (.in(L1_2_q));
  LED L1_4 (.in(L1_2_qn));
  LED L2_3 (.in(L2_2_q));
  LED L2_4 (.in(L2_2_qn));
endmodule
