// Logisim project 2.1.1.circ as structural Verilog: 1 circuit, main circuit main
module main (
  input  A,
  input  B,
  input  A_2,
  input  B_2,
  input  in_5,
  input  in_6,
  output AB,
  output A_B,
  output A_xor_B
);

  and and_1 (AB, A, B);
  or or_1 (A_B, A_2, B_2);
  xor xor_1 (A_xor_B, in_5, in_6);
endmodule
