// Logisim project 2.1.2.circ as structural Verilog: 1 circuit, main circuit main
module main (
  input  A,
  input  A_2,
  input  B,
  input  A_3,
  input  B_2,
  input  A_4,
  input  B_3,
  output out_8,
  output AB,
  output A_B,
  output n_A_xor_B
);

  Controlled_Inverter controlled_inverter_1 (.in(A), .out(out_8));  // open: en
  nand nand_1 (AB, A_2, B);
  nor nor_1 (A_B, A_3, B_2);
  xnor xnor_1 (n_A_xor_B, A_4, B_3);
endmodule
