// Logisim project 2.1.3.circ as structural Verilog: 1 circuit, main circuit main
module main (
  input  A,
  input  B,
  input  C,
  input  A_2,
  input  B_2,
  input  C_2,
  input  A_3,
  input  B_3,
  input  C_3,
  output ABC,
  output ABC_2,
  output ABC_3
);

  wire and_1_out, and_2_out;

  and and_1 (and_1_out, A, B);
  and and_2 (and_2_out, B_2, C_2);
  and and_3 (ABC_3, A_3, B_3, C_3);
  and and_4 (ABC, and_1_out, C);
  and and_5 (ABC_2, A_2, and_2_out);
endmodule
