// Logisim project 2.1.4.circ as structural Verilog: 1 circuit, main circuit main
module main (
  input  A,
  input  B,
  input  C,
  input  A_2,
  input  B_2,
  input  C_2,
  input  A_3,
  input  B_3,
  input  C_3,
  input  A_4,
  input  B_4,
  input  C_4,
  output F0,
  output F1,
  output F2,
  output F3
);

  wire and_1_out, and_2_out, and_3_out, or_1_out, or_2_out, or_3_out;

  or or_1 (or_1_out, A, B);
  and and_1 (and_1_out, A_2, C_2);
  and and_2 (and_2_out, B_2, C_2);
  and and_3 (and_3_out, A_3, B_3);
  or or_2 (or_2_out, A_4, C_4);
  or or_3 (or_3_out, B_4, C_4);
  and and_4 (F0, or_1_out, C);
  or or_4 (F1, and_1_out, and_2_out);
  or or_5 (F2, and_3_out, C_3);
  and and_5 (F3, or_2_out, or_3_out);
endmodule
