// Logisim project 2.2.1.circ as structural Verilog: 1 circuit, main circuit main
module main (
  input  in_1,
  input  in_2,
  input  X,
  input  Y,
  output out_5,
  output out_6
);

  wire and_1_out, and_2_out, and_3_out, not_1_out, not_2_out, not_3_out;

  not not_1 (not_1_out, in_1);
  not not_2 (not_2_out, X);
  not not_3 (not_3_out, Y);
  or or_1 (out_5, not_1_out, in_2);
  and and_1 (and_1_out, not_2_out, not_3_out);
  and and_2 (and_2_out, not_2_out, Y);
  and and_3 (and_3_out, X, Y);
  or or_2 (out_6, and_1_out, and_2_out, and_3_out);
endmodule
