// Logisim project 2.2.1B.circ as structural Verilog: 1 circuit, main circuit main
module main (
  input  A,
  input  B,
  input  C,
  output out_4
);

  wire and_1_out, and_2_out, and_3_out, and_4_out, not_1_out, not_2_out;

  not not_1 (not_1_out, A);
  not not_2 (not_2_out, B);
  // NOT_Gate not_3 has open pins: in=C, out=open
  and and_1 (and_1_out, not_1_out, B);
  buf and_2 (and_2_out, not_2_out);  // AND_Gate
  and and_3 (and_3_out, A, B);
  and and_4 (and_4_out, not_2_out, C);
  or or_1 (out_4, and_1_out, and_2_out, and_3_out, and_4_out);
endmodule
