// Logisim project 2.2.2B.circ as structural Verilog: 1 circuit, main circuit main
module main (
  input  A,
  input  B,
  input  C,
  output out_4
);

  wire and_1_out, not_1_out, not_2_out, not_3_out, or_1_out;

  not not_1 (not_1_out, A);
  not not_2 (not_2_out, B);
  not not_3 (not_3_out, C);
  or or_1 (or_1_out, not_1_out, not_2_out, not_3_out);
  and and_1 (and_1_out, A, B, C);
  and and_2 (out_4, or_1_out, and_1_out);
endmodule
