// Logisim project adder.circ as structural Verilog: 1 circuit, main circuit main
module main (
  input  A,
  input  B,
  input  Carry_in,
  output S1,
  output C
);

  wire and_1_out, and_2_out, xor_1_out;

  xor xor_1 (xor_1_out, A, B);
  and and_1 (and_1_out, A, B);
  xor xor_2 (S1, xor_1_out, Carry_in);
  or or_1 (C, and_1_out, and_2_out);
  and and_2 (and_2_out, xor_1_out, Carry_in);
endmodule
