// Logisim project 3 to 8 bit decoder.circ as structural Verilog: 1 circuit, main circuit main
module main (
  input  X,
  input  Y,
  input  Z,
  output _7,
  output _6,
  output _5,
  output _4,
  output _3,
  output _2,
  output _1,
  output _0
);

  wire not_1_out, not_2_out, not_3_out;

  not not_1 (not_1_out, X);
  not not_2 (not_2_out, Y);
  not not_3 (not_3_out, Z);
  and and_1 (_7, Z, Y, X);
  and and_2 (_6, not_3_out, Y, X);
  and and_3 (_5, Z, not_2_out, X);
  and and_4 (_3, Z, Y, not_1_out);
  and and_5 (_4, not_3_out, not_2_out, X);
  and and_6 (_1, Z, not_2_out, not_1_out);
  and and_7 (_2, not_3_out, Y, not_1_out);
  and and_8 (_0, not_3_out, not_2_out, not_1_out);
endmodule
