// Logisim project 4 bit adder(modified)for contraction.circ as structural Verilog: 2 circuits, main circuit main
module main (
  input  A,
  input  B,
  input  Carry_in,
  output S1,
  output C
);

  wire and_1_out, and_2_out, xor_1_out;

  xor xor_1 (xor_1_out, A, B);
  and and_1 (and_1_out, A, B);
  xor xor_2 (S1, xor_1_out, Carry_in);
  or or_1 (C, and_1_out, and_2_out);
  and and_2 (and_2_out, xor_1_out, Carry_in);
endmodule

module _4_Bit_Adder (
  input  [3:0] in_1,
  input  in_2,
  input  [3:0] in_3,
  output [1:0] S,
  output Cout
);

  wire main_1_c, main_2_c, main_3_c;
  wire [3:2] main_3_s1;

  main main_1 (.A(in_1[0]), .B(in_3[0]), .Carry_in(in_2), .S1(S[0]), .C(main_1_c));
  main main_2 (.A(in_1[1]), .B(in_3[1]), .Carry_in(main_1_c), .S1(S[1]), .C(main_2_c));
  main main_3 (.A(in_1[2]), .B(in_3[2]), .Carry_in(main_2_c), .S1(main_3_s1[2]), .C(main_3_c));
  main main_4 (.A(in_1[3]), .B(in_3[3]), .Carry_in(main_3_c), .S1(main_3_s1[3]), .C(Cout));
endmodule
