// Logisim project 4-bit square root.circ as structural Verilog: 1 circuit, main circuit main
module main (
  input  A,
  input  B,
  input  C,
  input  D
);

  wire and_1_out, and_2_out, and_3_out, and_4_out, and_5_out, and_6_out, and_7_out, and_8_out, and_9_out,
       and_10_out, and_11_out, not_1_out, not_2_out, not_3_out, not_4_out, or_1_out, or_2_out, or_3_out;

  not not_1 (not_1_out, A);
  not not_2 (not_2_out, B);
  not not_3 (not_3_out, C);
  not not_4 (not_4_out, D);
  and and_1 (and_1_out, A, B, D);
  and and_2 (and_2_out, A, B, C);
  and and_3 (and_3_out, not_2_out, C, D);
  and and_4 (and_4_out, A, not_3_out, not_4_out);
  and and_5 (and_5_out, not_1_out, B);
  and and_6 (and_6_out, A, not_2_out);
  and and_7 (and_7_out, A, not_2_out);
  and and_8 (and_8_out, A, not_3_out, not_4_out);
  and and_9 (and_9_out, C, not_2_out, not_4_out);
  and and_10 (and_10_out, not_2_out, not_3_out, D);
  and and_11 (and_11_out, not_1_out, B, C, D);
  or or_1 (or_1_out, and_1_out, and_2_out);
  LED F2 (.in(or_1_out));
  LED F1 (.in(or_2_out));
  or or_2 (or_2_out, and_3_out, and_4_out, and_5_out, and_6_out);
  or or_3 (or_3_out, and_7_out, and_8_out, and_9_out, and_10_out, and_11_out);
  LED F0 (.in(or_3_out));
endmodule
