// Logisim project Tail Light design problem Part B.circ as structural Verilog: 1 circuit, main circuit main
module main (
  input  LT,
  input  RT,
  input  BR,
  input  ED
);

  wire and_1_out, and_2_out, and_3_out, and_4_out, and_5_out, clock_1_out, decoder_1_out1, decoder_1_out2,
       decoder_1_out4, decoder_1_out5, decoder_1_out6, decoder_1_out8, decoder_1_out12, or_1_out, xor_1_out,
       xor_2_out;

  LED LR (.in(xor_1_out));
  LED RR (.in(xor_2_out));
  ExactlyOne xor_1 (.out(xor_1_out), .in0(and_1_out), .in1(and_2_out), .in2(and_3_out), .in3(or_1_out));
  ExactlyOne xor_2 (.out(xor_2_out), .in0(and_3_out), .in1(or_1_out), .in2(and_4_out), .in3(and_5_out));
  and and_1 (and_1_out, clock_1_out, decoder_1_out5);
  and and_2 (and_2_out, clock_1_out, decoder_1_out1);
  and and_3 (and_3_out, clock_1_out, decoder_1_out8);
  and and_4 (and_4_out, clock_1_out, decoder_1_out2);
  and and_5 (and_5_out, clock_1_out, decoder_1_out6);
  Clock clock_1 (.out(clock_1_out));
  or or_1 (or_1_out, decoder_1_out4, decoder_1_out12);
  Decoder #(.select(4), .enable("false")) decoder_1 (
    .out1(decoder_1_out1), .out2(decoder_1_out2), .out4(decoder_1_out4), .out5(decoder_1_out5),
    .out6(decoder_1_out6), .out8(decoder_1_out8), .out12(decoder_1_out12), .sel({ED, BR, RT, LT}));  // open: out0, out3, out7, out9, out10, out11, out13, out14, out15
endmodule
