// Logisim project Tail Light design problem..circ as structural Verilog: 1 circuit, main circuit main
module main (
  input  LT,
  input  RT,
  input  BR,
  input  ED
);

  wire and_1_out, and_2_out, and_3_out, and_4_out, and_5_out, and_6_out, BL_out, not_1_out, not_2_out,
       not_3_out, not_4_out, or_1_out, or_2_out, xor_1_out, xor_2_out;

  not not_1 (not_1_out, LT);
  not not_2 (not_2_out, RT);
  not not_3 (not_3_out, BR);
  not not_4 (not_4_out, ED);
  Clock BL (.out(BL_out));
  and and_1 (and_1_out, LT, not_2_out, not_3_out, not_4_out);
  and and_2 (and_2_out, not_1_out, RT, not_3_out, not_4_out);
  and and_3 (and_3_out, BR, not_4_out);
  and and_4 (and_4_out, BL_out, and_1_out);
  and and_5 (and_5_out, and_2_out, BL_out);
  and and_6 (and_6_out, BL_out, ED);
  or or_1 (or_1_out, and_4_out, and_3_out);
  or or_2 (or_2_out, and_5_out, and_3_out);
  LED LR (.in(xor_1_out));
  xor xor_1 (xor_1_out, or_1_out, and_6_out);
  LED RR (.in(xor_2_out));
  xor xor_2 (xor_2_out, or_2_out, and_6_out);
endmodule
