// Logisim project 2bit inverter.circ as structural Verilog: 1 circuit, main circuit main
module main (
  input  [1:0] in_1,
  output [1:0] out_2
);

  wire not_1_out, not_2_out;
  wire [1:0] main_1_c;

  not not_1 (not_1_out, in_1[0]);
  not not_2 (not_2_out, in_1[1]);
  Multiplexer #(.width(2), .enable("false")) multiplexer_1 (.in0(in_1), .in1(main_1_c), .out(out_2), .sel(1'b1));
  _4_bit_adder_modified__main main_1 (.A(not_1_out), .B(1'b1), .Carry_in(1'b0), .C(main_1_c[0]));  // open: S1
  _4_bit_adder_modified__main main_2 (.A(not_2_out), .B(1'b1), .Carry_in(1'b0), .C(main_1_c[1]));  // open: S1
endmodule
