// Logisim project 4.2.1.circ as structural Verilog: 1 circuit, main circuit main
module main (
  input  B3,
  input  B2,
  input  B1,
  input  B0
);

  wire and_1_out, and_2_out, and_3_out, and_4_out, and_5_out, and_6_out, and_7_out, and_8_out, nand_1_out,
       nand_2_out, nand_3_out, nand_4_out, nand_5_out, nand_6_out, nand_7_out, nand_8_out, nand_9_out,
       nand_10_out, nand_11_out, nand_12_out, nand_13_out, nand_14_out, not_1_out, or_1_out, xor_1_out,
       xor_2_out;

  and and_1 (and_1_out, ~B3, B2);  // AND_Gate
  xor xor_1 (xor_1_out, B1, B0);
  nand nand_1 (nand_1_out, and_1_out, xor_1_out);
  _7_Segment_Display u_7_segment_display_1 (
    .g(and_8_out), .f(and_6_out), .a(not_1_out), .b(nand_1_out), .e(or_1_out), .d(and_7_out), .c(nand_14_out));  // open: dp
  and and_2 (and_2_out, B3, ~B2, ~B1, ~B0);  // AND_Gate
  nand nand_2 (nand_2_out, ~B3, ~B2, ~B1, B0);  // NAND_Gate
  or or_1 (or_1_out, and_2_out, and_3_out, and_4_out, and_5_out);
  and and_3 (and_3_out, ~B3, B2, B1, ~B0);  // AND_Gate
  nand nand_3 (nand_3_out, ~B3, B2, ~B1, ~B0);  // NAND_Gate
  xor xor_2 (xor_2_out, nand_2_out, nand_3_out);
  not not_1 (not_1_out, xor_2_out);
  and and_4 (and_4_out, ~B3, ~B2, B1, ~B0);  // AND_Gate
  nand nand_4 (nand_4_out, ~B3, ~B2, ~B1, B0);  // NAND_Gate
  and and_5 (and_5_out, ~B3, ~B2, ~B1, ~B0);  // AND_Gate
  nand nand_5 (nand_5_out, ~B3, ~B2, B1, ~B0);  // NAND_Gate
  and and_6 (and_6_out, nand_4_out, nand_5_out, nand_8_out, nand_7_out);
  nand nand_6 (nand_6_out, ~B3, B2, B1, B0);  // NAND_Gate
  nand nand_7 (nand_7_out, ~B3, B2, B1, B0);  // NAND_Gate
  nand nand_8 (nand_8_out, ~B3, ~B2, B1, B0);  // NAND_Gate
  and and_7 (and_7_out, nand_6_out, nand_9_out, nand_11_out);
  nand nand_9 (nand_9_out, ~B3, B2, ~B1, ~B0);  // NAND_Gate
  nand nand_10 (nand_10_out, ~B3, ~B2, ~B1, ~B0);  // NAND_Gate
  nand nand_11 (nand_11_out, ~B3, ~B2, ~B1, B0);  // NAND_Gate
  nand nand_12 (nand_12_out, ~B3, ~B2, ~B1, B0);  // NAND_Gate
  and and_8 (and_8_out, nand_10_out, nand_12_out, nand_13_out);
  nand nand_13 (nand_13_out, ~B3, B2, B1, B0);  // NAND_Gate
  nand nand_14 (nand_14_out, ~B3, ~B2, B1, ~B0);  // NAND_Gate
endmodule
