// Logisim project 4.2.2.circ as structural Verilog: 1 circuit, main circuit main
module main (
  input  SEL,
  input  A0,
  input  B0,
  input  A1,
  input  B1,
  input  A2,
  input  B2,
  input  A3,
  input  B3,
  output M0,
  output M1,
  output M2,
  output M3
);

  wire and_1_out, and_2_out, and_3_out, and_4_out, and_5_out, and_6_out, and_7_out, and_8_out, not_1_out;

  not not_1 (not_1_out, SEL);
  and and_1 (and_1_out, A0, not_1_out);
  and and_2 (and_2_out, B0, SEL);
  and and_3 (and_3_out, A1, not_1_out);
  and and_4 (and_4_out, B1, SEL);
  and and_5 (and_5_out, A2, not_1_out);
  and and_6 (and_6_out, B2, SEL);
  and and_7 (and_7_out, A3, not_1_out);
  and and_8 (and_8_out, B3, SEL);
  or or_1 (M0, and_1_out, and_2_out);
  or or_2 (M1, and_3_out, and_4_out);
  or or_3 (M2, and_5_out, and_6_out);
  or or_4 (M3, and_7_out, and_8_out);
endmodule
