// Logisim project 4.2.3.circ as structural Verilog: 1 circuit, main circuit main
module main (
  input  A,
  input  B,
  input  C,
  output out_4,
  output out_5
);

  wire decoder_1_out1, decoder_1_out2, decoder_1_out3, decoder_1_out4, decoder_1_out5, decoder_1_out6,
       decoder_1_out7;

  Decoder #(.select(3), .enable("false")) decoder_1 (
    .out1(decoder_1_out1), .out2(decoder_1_out2), .out3(decoder_1_out3), .out4(decoder_1_out4),
    .out5(decoder_1_out5), .out6(decoder_1_out6), .out7(decoder_1_out7), .sel({A, B, C}));  // open: out0
  or u_C (out_5, decoder_1_out3, decoder_1_out5, decoder_1_out6, decoder_1_out7);
  or or_1 (out_4, decoder_1_out1, decoder_1_out2, decoder_1_out4, decoder_1_out7);
endmodule
