// Logisim project 8 bit adder subtractor thing.circ as structural Verilog: 1 circuit, main circuit main
module main (
  input  [3:0] in_1,
  input  SA,
  output [1:0] out_3,
  output out_4
);

  wire [3:0] main_1_out_2, multiplexer_1_out;

  Inverter_main main_1 (.in_1(4'b0010), .out_2(main_1_out_2));
  Multiplexer #(.width(4), .enable("false")) multiplexer_1 (
    .in0(4'b0010), .in1(main_1_out_2), .out(multiplexer_1_out), .sel(SA));
  _4_Bit_Adder u_4_bit_adder_1 (.in_1(multiplexer_1_out), .in_2(1'b0), .in_3(in_1), .S(out_3), .Cout(out_4));
  // _4_bit_adder_modified_for_contraction_main main_2: pin names not known
endmodule
