// Logisim project Gray.circ as structural Verilog: 1 circuit, main circuit Gray
module Gray (
  input  CLK,
  output [3:0] GRAY
);

  wire [3:0] counter_1_q;

  Counter #(.width(4), .max('hf)) counter_1 (.Q(counter_1_q), .clk(CLK));  // open: load, D, count, carry, clr
  Multiplexer #(.select(4), .width(4), .enable("false")) multiplexer_1 (
    .in0(4'b0000), .in1(4'b0001), .in2(4'b0011), .in3(4'b0010), .in4(4'b0110), .in5(4'b0111), .in6(4'b0101),
    .in7(4'b0100), .in8(4'b1100), .in9(4'b1101), .in10(4'b1111), .in11(4'b1110), .in12(4'b1010),
    .in13(4'b1011), .in14(4'b1001), .in15(4'b1000), .out(GRAY), .sel(counter_1_q));
endmodule
