// Logisim project Inverter.circ as structural Verilog: 1 circuit, main circuit main
module main (
  input  [3:0] in_1,
  output [3:0] out_2
);

  wire [3:0] n4_bit_adder_1_s, not_1_out;

  not not_1 (not_1_out[0], in_1[0]);
  not not_2 (not_1_out[1], in_1[1]);
  not not_3 (not_1_out[2], in_1[2]);
  not not_4 (not_1_out[3], in_1[3]);
  Multiplexer #(.width(4), .enable("false")) multiplexer_1 (
    .in0(in_1), .in1(n4_bit_adder_1_s), .out(out_2), .sel(1'b1));
  _4_Bit_Adder u_4_bit_adder_1 (.in_1(not_1_out), .in_2(1'b1), .in_3(4'b0000), .S(n4_bit_adder_1_s));  // open: Cout
endmodule
