// Logisim project Traffic Lights.circ as structural Verilog: 1 circuit, main circuit main
module main (
);

  wire and_1_out, and_2_out, and_3_out, and_4_out, and_5_out, and_6_out, and_7_out, and_8_out, clock_1_out,
       not_1_out, or_1_out, or_2_out, or_3_out, or_4_out;
  wire [3:0] gray_1_gray;

  Clock #(.highDuration(5)) clock_1 (.out(clock_1_out));
  Gray gray_1 (.CLK(clock_1_out), .GRAY(gray_1_gray));
  and and_1 (and_1_out, ~gray_1_gray[3], ~gray_1_gray[2]);  // AND_Gate
  and and_2 (and_2_out, gray_1_gray[0], gray_1_gray[3]);
  and and_3 (and_3_out, gray_1_gray[3], ~gray_1_gray[2], ~gray_1_gray[1], ~gray_1_gray[0]);  // AND_Gate
  and and_4 (and_4_out, ~gray_1_gray[3], gray_1_gray[1]);  // AND_Gate
  and and_5 (and_5_out, gray_1_gray[3], gray_1_gray[1]);
  or or_1 (or_1_out, and_2_out, and_5_out);
  and and_6 (and_6_out, ~gray_1_gray[3], gray_1_gray[2], gray_1_gray[0], ~gray_1_gray[1]);  // AND_Gate
  not not_1 (not_1_out, gray_1_gray[3]);
  and and_7 (and_7_out, gray_1_gray[2], ~gray_1_gray[1], ~gray_1_gray[0]);  // AND_Gate
  or or_2 (or_2_out, not_1_out, and_7_out);
  and and_8 (and_8_out, gray_1_gray[2], ~gray_1_gray[1], ~gray_1_gray[0]);  // AND_Gate
  LED RNS (.in(or_2_out));
  LED GNS (.in(or_1_out));
  LED YNS (.in(and_3_out));
  or or_3 (or_3_out, and_8_out, gray_1_gray[3]);
  LED REW (.in(or_3_out));
  LED YEW (.in(and_6_out));
  LED GEW (.in(or_4_out));
  or or_4 (or_4_out, and_4_out, and_1_out);
endmodule
