// Logisim project add-sub.circ as structural Verilog: 1 circuit, main circuit main
module main (
  input  [3:0] in_1,
  input  [3:0] in_2,
  input  SA,
  output [3:0] out_4,
  output out_5
);

  wire [3:0] main_1_out_2, multiplexer_1_out;

  Inverter_main main_1 (.in_1(in_1), .out_2(main_1_out_2));
  Multiplexer #(.width(4), .enable("false")) multiplexer_1 (
    .in0(in_1), .in1(main_1_out_2), .out(multiplexer_1_out), .sel(SA));
  _4_Bit_Adder u_4_bit_adder_1 (.in_1(multiplexer_1_out), .in_2(1'b0), .in_3(in_2), .S(out_4), .Cout(out_5));
endmodule
