// Logisim project 5.1.2.circ as structural Verilog: 1 circuit, main circuit main
module main (
  input  [2:0] in_1,
  input  [2:0] in_2,
  output _14,
  output _13,
  output _12,
  output _11,
  output _10,
  output _9,
  output _8,
  output _7,
  output _6,
  output _5,
  output _4,
  output _3,
  output _2,
  output _1,
  output _0
);

  wire decoder_1_out0, decoder_1_out1, decoder_1_out2, decoder_1_out3, decoder_1_out4, decoder_1_out5,
       decoder_1_out6, decoder_1_out7, decoder_2_out0, decoder_2_out1, decoder_2_out2, decoder_2_out3,
       decoder_2_out4, decoder_2_out5, decoder_2_out6, decoder_2_out7;

  Decoder #(.select(3), .enable("false")) decoder_1 (
    .out0(decoder_1_out0), .out1(decoder_1_out1), .out2(decoder_1_out2), .out3(decoder_1_out3),
    .out4(decoder_1_out4), .out5(decoder_1_out5), .out6(decoder_1_out6), .out7(decoder_1_out7), .sel(in_1));
  Decoder #(.select(3), .enable("false")) decoder_2 (
    .out0(decoder_2_out0), .out1(decoder_2_out1), .out2(decoder_2_out2), .out3(decoder_2_out3),
    .out4(decoder_2_out4), .out5(decoder_2_out5), .out6(decoder_2_out6), .out7(decoder_2_out7), .sel(in_2));
  and and_1 (_14, decoder_2_out7, decoder_1_out7);
  and and_2 (_13, decoder_2_out6, decoder_1_out7);
  and and_3 (_12, decoder_2_out5, decoder_1_out7);
  and and_4 (_11, decoder_2_out4, decoder_1_out7);
  and and_5 (_10, decoder_2_out3, decoder_1_out7);
  and and_6 (_8, decoder_2_out1, decoder_1_out7);
  and and_7 (_9, decoder_2_out2, decoder_1_out7);
  and and_8 (_7, decoder_1_out7, decoder_2_out0);
  and and_9 (_6, decoder_1_out6, decoder_2_out0);
  and and_10 (_5, decoder_1_out5, decoder_2_out0);
  and and_11 (_4, decoder_1_out4, decoder_2_out0);
  and and_12 (_2, decoder_2_out0, decoder_1_out2);
  and and_13 (_3, decoder_2_out0, decoder_1_out3);
  and and_14 (_0, decoder_2_out0, decoder_1_out0);
  and and_15 (_1, decoder_2_out0, decoder_1_out1);
endmodule
