// Logisim project 5.1.3.circ as structural Verilog: 1 circuit, main circuit main
module main (
  input  A,
  input  B,
  input  C,
  input  D,
  output F0,
  output F1
);

  wire not_1_out;

  not not_1 (not_1_out, A);
  Part_one_of_5_1_3_main main_1 (.A(not_1_out), .B(B), .C(C), .D(D), .F0(F0));
  Part_two_of_5_1_3_main main_2 (.A(A), .B(B), .C(C), .D(D), .F1(F1));
endmodule
