// Logisim project 5.1.4.circ as structural Verilog: 1 circuit, main circuit main
module main (
  input  [2:0] in_1,
  output _5,
  output _4,
  output _3,
  output _2,
  output _1,
  output _0
);

  wire decoder_1_out0, decoder_1_out1, decoder_2_out0, decoder_2_out1, decoder_2_out2, decoder_2_out3;

  Decoder #(.enable("false")) decoder_1 (.out0(decoder_1_out0), .out1(decoder_1_out1), .sel(in_1[2]));
  Decoder #(.select(2), .enable("false")) decoder_2 (
    .out0(decoder_2_out0), .out1(decoder_2_out1), .out2(decoder_2_out2), .out3(decoder_2_out3),
    .sel(in_1[1:0]));
  and and_1 (_5, decoder_1_out1, decoder_2_out1);
  and and_2 (_4, decoder_2_out0, decoder_1_out1);
  and and_3 (_2, decoder_2_out2, decoder_1_out0);
  and and_4 (_3, decoder_2_out3, decoder_1_out0);
  and and_5 (_0, decoder_2_out0, decoder_1_out0);
  and and_6 (_1, decoder_2_out1, decoder_1_out0);
endmodule
