// Logisim project 5.2.2.circ as structural Verilog: 1 circuit, main circuit main
module main (
  input  in_1,
  input  in_2,
  input  in_3,
  input  in_4,
  input  in_5,
  input  in_6,
  input  in_7,
  input  in_8,
  input  A,
  input  B,
  input  C,
  input  D,
  output out_13
);

  wire multiplexer_1_out, multiplexer_2_out;

  Multiplexer #(.select(2), .enable("false")) multiplexer_1 (
    .in0(in_1), .in1(in_2), .in2(in_3), .in3(in_4), .out(multiplexer_1_out), .sel({B, A}));
  Multiplexer #(.select(2), .enable("false")) multiplexer_2 (
    .in0(in_5), .in1(in_6), .in2(in_7), .in3(in_8), .out(multiplexer_2_out), .sel({D, C}));
  Multiplexer #(.enable("false")) multiplexer_3 (
    .in0(multiplexer_1_out), .in1(multiplexer_2_out), .out(out_13), .sel(multiplexer_2_out));
endmodule
