// Logisim project 5.2.3.circ as structural Verilog: 1 circuit, main circuit main
module main (
  input  [1:0] in_1,
  input  in_2,
  input  in_3,
  output out_4
);

  wire and_1_out, and_2_out, and_3_out, and_4_out;

  and and_1 (and_1_out, ~in_1[1], ~in_1[0], in_3);  // AND_Gate
  and and_2 (and_2_out, in_1[0], ~in_2, ~in_3);  // AND_Gate
  and and_3 (and_3_out, in_1[1], in_2, in_3);
  and and_4 (and_4_out, in_1[0], in_1[1]);
  Multiplexer #(.select(2), .enable("false")) multiplexer_1 (
    .in0(and_1_out), .in1(and_2_out), .in2(and_3_out), .in3(and_4_out), .out(out_4), .sel(in_1));
endmodule
