// Logisim project 5.2.4.circ as structural Verilog: 1 circuit, main circuit main
module main (
  input  [1:0] in_1,
  input  C,
  input  D,
  output out_4
);

  wire and_1_out, and_2_out, and_3_out, and_4_out, and_5_out, and_6_out, or_1_out, or_2_out, xor_1_out;

  and and_1 (and_1_out, C, D);
  and and_2 (and_2_out, ~C, D);  // AND_Gate
  or or_1 (or_1_out, and_1_out, and_2_out);
  and and_3 (and_3_out, ~C, ~D);  // AND_Gate
  and and_4 (and_4_out, C, D);
  xor xor_1 (xor_1_out, C, D);
  and and_5 (and_5_out, C, D);
  or or_2 (or_2_out, and_5_out, xor_1_out, and_6_out);
  and and_6 (and_6_out, ~C, ~D);  // AND_Gate
  Multiplexer #(.select(2), .enable("false")) multiplexer_1 (
    .in0(or_2_out), .in1(and_4_out), .in2(and_3_out), .in3(or_1_out), .out(out_4), .sel(in_1));
endmodule
