// Logisim project 5.2.5 Dice.circ as structural Verilog: 1 circuit, main circuit main
module main (
  input  [2:0] in_1
);

  wire decoder_1_out1, decoder_1_out2, decoder_1_out3, decoder_1_out4, decoder_1_out5, decoder_1_out6,
       or_1_out, or_2_out, or_3_out;

  LED A (.in(or_1_out));
  LED C (.in(decoder_1_out6));
  LED F (.in(or_2_out));
  LED B (.in(or_2_out));
  LED E (.in(decoder_1_out6));
  LED D (.in(or_3_out));
  LED G (.in(or_1_out));
  or or_1 (or_1_out, decoder_1_out2, decoder_1_out3, decoder_1_out4, decoder_1_out5, decoder_1_out6);
  or or_2 (or_2_out, decoder_1_out4, decoder_1_out5, decoder_1_out6);
  or or_3 (or_3_out, decoder_1_out1, decoder_1_out3, decoder_1_out5);
  Decoder #(.select(3), .enable("false")) decoder_1 (
    .out1(decoder_1_out1), .out2(decoder_1_out2), .out3(decoder_1_out3), .out4(decoder_1_out4),
    .out5(decoder_1_out5), .out6(decoder_1_out6), .sel(in_1));  // open: out0, out7
endmodule
