// Logisim project Part two of 5.1.3.circ as structural Verilog: 1 circuit, main circuit main
module main (
  input  A,
  input  B,
  input  C,
  input  D,
  output F1
);

  wire and_1_out, and_2_out;

  and and_1 (and_1_out, A, ~B, ~C);  // AND_Gate
  and and_2 (and_2_out, A, B, ~D);  // AND_Gate
  or or_1 (F1, and_1_out, and_2_out);
endmodule
