// Logisim project 7.2.circ as structural Verilog: 1 circuit, main circuit main
module main (
  input  X,
  output Y
);

  wire and_1_out, and_2_out, and_3_out, and_4_out, and_5_out, and_6_out, and_7_out, and_8_out, and_9_out,
       and_10_out, and_11_out, and_12_out, and_13_out, and_14_out, clock_1_out, not_1_out, or_1_out,
       or_2_out, or_3_out, SA_q, SA_qn, SB_q, SB_qn, SC_q, SC_qn, xor_1_out;

  Clock clock_1 (.out(clock_1_out));
  not not_1 (not_1_out, X);
  and and_1 (and_1_out, SA_q, SB_qn, SC_qn);
  and and_2 (and_2_out, SB_qn, X);
  D_Flip_Flop SA (.clk(clock_1_out), .D(or_1_out), .Q(SA_q), .Qn(SA_qn));  // open: preset, en, reset
  or or_1 (or_1_out, and_1_out, and_2_out);
  and and_3 (and_3_out, SC_q, not_1_out);
  and and_4 (and_4_out, SB_q, SC_q);
  and and_5 (and_5_out, SA_q, SC_q);
  D_Flip_Flop SB (.clk(clock_1_out), .D(or_2_out), .Q(SB_q), .Qn(SB_qn));  // open: preset, en, reset
  or or_2 (or_2_out, and_3_out, and_4_out, and_5_out);
  and and_6 (and_6_out, ~X, SB_qn);  // AND_Gate
  xor xor_1 (xor_1_out, and_6_out, and_8_out);
  and and_7 (and_7_out, SA_qn, xor_1_out);
  and and_8 (and_8_out, SB_q, X);
  and and_9 (and_9_out, SA_q, SB_qn, SC_qn);
  and and_10 (and_10_out, SA_qn, SB_qn, SC_q);
  and and_11 (and_11_out, SB_qn, SC_qn, ~X);  // AND_Gate
  and and_12 (and_12_out, SA_q, SB_qn, SC_qn, X);
  D_Flip_Flop SC (.clk(clock_1_out), .D(or_3_out), .Q(SC_q), .Qn(SC_qn));  // open: preset, en, reset
  or or_3 (or_3_out, and_9_out, and_10_out, and_11_out);
  and and_13 (and_13_out, SA_q, SB_q, ~X);  // AND_Gate
  or or_4 (Y, and_14_out, and_13_out, and_12_out, and_7_out);
  and and_14 (and_14_out, SA_q, SC_q, ~X);  // AND_Gate
endmodule
