// Logisim project 7.3 alternate.circ as structural Verilog: 1 circuit, main circuit main
module main (
  input  [7:0] IN,
  input  Shift,
  input  Reset,
  output [7:0] OUT
);

  wire clock_1_out, main_1_y, not_1_out, shift_register_1_out;
  wire [7:0] shift_register_2_q7;

  Clock clock_1 (.out(clock_1_out));
  not not_1 (not_1_out, Shift);
  Shift_Register shift_register_1 (
    .shift(Shift), .in(1'b0), .clk(clock_1_out), .out(shift_register_1_out), .load(not_1_out), .clr(Reset),
    .d0(IN[7]), .d1(IN[6]), .d2(IN[5]), .d3(IN[4]), .d4(IN[3]), .d5(IN[2]), .d6(IN[1]), .d7(IN[0]));  // open: q0, q1, q2, q3, q4, q5, q6, q7
  _7_2_main main_1 (.X(shift_register_1_out), .Y(main_1_y));
  Shift_Register #(.trigger("falling")) shift_register_2 (
    .shift(Shift), .in(main_1_y), .clk(clock_1_out), .q0(shift_register_2_q7[7]),
    .q1(shift_register_2_q7[6]), .q2(shift_register_2_q7[5]), .q3(shift_register_2_q7[4]),
    .q4(shift_register_2_q7[3]), .q5(shift_register_2_q7[2]), .q6(shift_register_2_q7[1]),
    .q7(shift_register_2_q7[0]));  // open: out, load, clr, d0, d1, d2, d3, d4, d5, d6, d7
  assign OUT = ~shift_register_2_q7;  // NOT_Gate not_2, 8 bits wide
endmodule
