// Logisim project 8.1.4.circ as structural Verilog: 1 circuit, main circuit main
module main (
);

  wire and_1_out, and_2_out, and_3_out, and_4_out, and_5_out, and_6_out, and_7_out, Dime_out, Nickel_out,
       or_1_out, or_2_out, or_3_out, S0_q, S0_qn, S1_q, S1_qn, xor_1_out;

  xor xor_1 (xor_1_out, Dime_out, Nickel_out);
  Button Dime (.out(Dime_out));
  Button Nickel (.out(Nickel_out));
  and and_1 (and_1_out, Nickel_out, ~Dime_out, S0_q, S1_qn);  // AND_Gate
  and and_2 (and_2_out, Dime_out, ~Nickel_out, S0_qn, S1_qn);  // AND_Gate
  or or_1 (or_1_out, and_1_out, and_2_out);
  D_Flip_Flop #(.trigger("falling")) S1 (
    .clk(xor_1_out), .D(or_1_out), .Q(S1_q), .Qn(S1_qn));  // open: preset, en, reset
  and and_3 (and_3_out, xor_1_out, S1_qn, S0_qn);
  and and_4 (and_4_out, S1_qn, S0_q, ~Dime_out, Nickel_out);  // AND_Gate
  and and_5 (and_5_out, S1_q, S0_q, Dime_out, ~Nickel_out);  // AND_Gate
  or or_2 (or_2_out, and_3_out, and_4_out);
  and and_6 (and_6_out, S1_qn, S0_q, Dime_out, ~Nickel_out);  // AND_Gate
  LED Happy_Face (.in(and_5_out));
  D_Flip_Flop #(.trigger("falling")) S0 (
    .clk(xor_1_out), .D(or_2_out), .Q(S0_q), .Qn(S0_qn));  // open: preset, en, reset
  and and_7 (and_7_out, S1_q, S0_q, xor_1_out);
  or or_3 (or_3_out, and_7_out, and_6_out);
  LED Product (.in(or_3_out));
endmodule
