// Logisim project 8.2.circ as structural Verilog: 4 circuits, main circuit main
module main (
  output [3:0] out_1,
  output Unlocked
);

  wire _1_out, _2_out, _3_out, _4_out, _5_out, _6_out, _7_out, _8_out, _9_out, and_1_out, counter_1_d0,
       counter_1_d1, d_ff_1_q, equality_comparator_1_out_3, n5_bit_thing_1_out_11, not_1_out;
  wire [1:0] counter_1_out_5;
  wire [3:0] rom_1_data;

  Button _1 (.out(_1_out));
  Button _2 (.out(_2_out));
  Button _3 (.out(_3_out));
  Button _4 (.out(_4_out));
  Button _5 (.out(_5_out));
  Button _6 (.out(_6_out));
  Button _7 (.out(_7_out));
  Button _8 (.out(_8_out));
  Button _9 (.out(_9_out));
  _5_bit_thing u_5_bit_thing_1 (
    ._1(_1_out), ._2(_2_out), ._3(_3_out), ._4(_4_out), ._5(_5_out), ._6(_6_out), ._7(_7_out), ._8(_8_out),
    ._9(_9_out), .out_10(out_1), .out_11(n5_bit_thing_1_out_11));
  Counter counter_1 (
    .Clock(n5_bit_thing_1_out_11), .D1(counter_1_d1), .D0(counter_1_d0), .out_5(counter_1_out_5),
    .Reset(d_ff_1_q));
  ROM #(.addrWidth(2), .dataWidth(4)) rom_1 (.addr(counter_1_out_5), .data(rom_1_data));  // open: sel
  not not_1 (not_1_out, equality_comparator_1_out_3);
  Equality_comparator equality_comparator_1 (.in_1(out_1), .in_2(rom_1_data), .out_3(equality_comparator_1_out_3));
  and and_1 (and_1_out, counter_1_d1, equality_comparator_1_out_3, counter_1_d0);
  D_Flip_Flop #(.trigger("falling")) d_ff_1 (
    .clk(n5_bit_thing_1_out_11), .D(not_1_out), .Q(d_ff_1_q), .reset(d_ff_1_q));  // open: Qn, preset, en
  D_Flip_Flop #(.trigger("falling")) d_ff_2 (
    .clk(n5_bit_thing_1_out_11), .D(and_1_out), .Q(Unlocked));  // open: Qn, preset, en, reset

  // Notes on the sheet:
  //   contents of rom_1 (hex, n*v repeats v):
  //   4 5 2 8
endmodule

module _5_bit_thing (
  input  _1,
  input  _2,
  input  _3,
  input  _4,
  input  _5,
  input  _6,
  input  _7,
  input  _8,
  input  _9,
  output [3:0] out_10,
  output out_11
);

  or or_1 (out_10[3], _8, _9);
  or or_2 (out_10[2], _7, _6, _5, _4);
  or or_3 (out_10[1], _7, _6, _3, _2);
  or or_4 (out_10[0], _1, _3, _5, _7, _9);
  or or_5 (out_11, _1, _2, _3, _4, _5, _6, _7, _8, _9);
endmodule

module Equality_comparator (
  input  [3:0] in_1,
  input  [3:0] in_2,
  output out_3
);

  wire and_1_out, and_2_out, and_3_out, and_4_out, nand_1_out, nand_2_out, nand_3_out, nand_4_out,
       nand_5_out, nand_6_out, nand_7_out, nand_8_out;

  nand nand_1 (nand_1_out, ~in_1[0], in_2[0]);  // NAND_Gate
  nand nand_2 (nand_2_out, ~in_2[0], in_1[0]);  // NAND_Gate
  nand nand_3 (nand_3_out, ~in_1[1], in_2[1]);  // NAND_Gate
  nand nand_4 (nand_4_out, ~in_2[1], in_1[1]);  // NAND_Gate
  nand nand_5 (nand_5_out, ~in_1[2], in_2[2]);  // NAND_Gate
  nand nand_6 (nand_6_out, ~in_2[2], in_1[2]);  // NAND_Gate
  nand nand_7 (nand_7_out, ~in_1[3], in_2[3]);  // NAND_Gate
  nand nand_8 (nand_8_out, ~in_2[3], in_1[3]);  // NAND_Gate
  and and_1 (and_1_out, nand_1_out, nand_2_out);
  and and_2 (and_2_out, nand_3_out, nand_4_out);
  and and_3 (and_3_out, nand_5_out, nand_6_out);
  and and_4 (and_4_out, nand_7_out, nand_8_out);
  and and_5 (out_3, and_1_out, and_2_out, and_3_out, and_4_out);
endmodule

module Counter (
  input  Clock,
  input  Reset,
  output D1,
  output D0,
  output [1:0] out_5
);

  wire and_1_out, and_2_out, and_3_out, and_4_out, D0_qn, D1_qn, or_1_out, or_2_out;

  and and_1 (and_1_out, D1_qn, D0);
  or or_1 (or_1_out, and_1_out, and_2_out);
  and and_2 (and_2_out, D1, D0_qn);
  and and_3 (and_3_out, D0_qn, D1_qn);
  and and_4 (and_4_out, D1, D0_qn);
  D_Flip_Flop #(.trigger("falling")) u_D1 (
    .clk(Clock), .D(or_1_out), .Q(D1), .Qn(D1_qn), .reset(Reset));  // open: preset, en
  or or_2 (or_2_out, and_3_out, and_4_out);
  D_Flip_Flop #(.trigger("falling")) u_D0 (
    .clk(Clock), .D(or_2_out), .Q(D0), .Qn(D0_qn), .reset(Reset));  // open: preset, en

  assign out_5 = {D1, D0};
endmodule
