// Logisim project 8.3.circ as structural Verilog: 1 circuit, main circuit main
module main (
  input  LEFT,
  input  RIGHT,
  input  HAZARD
);

  wire and_1_out, and_2_out, and_3_out, and_4_out, and_5_out, and_6_out, and_7_out, and_8_out, and_9_out,
       and_10_out, clock_1_out, LA_qn, LB_q, LC_q, or_1_out, or_2_out, or_3_out, or_4_out, or_5_out,
       or_6_out, RA_qn, RB_q, RC_q;

  and and_1 (and_1_out, LEFT, ~RIGHT, ~HAZARD);  // AND_Gate
  and and_2 (and_2_out, ~LEFT, RIGHT, ~HAZARD);  // AND_Gate
  and and_3 (and_3_out, ~LEFT, RIGHT, ~HAZARD);  // AND_Gate
  and and_4 (and_4_out, LEFT, ~RIGHT, ~HAZARD);  // AND_Gate
  Clock clock_1 (.out(clock_1_out));
  or or_1 (or_1_out, and_1_out, HAZARD);
  or or_2 (or_2_out, and_2_out, HAZARD);
  D_Flip_Flop LC (.clk(clock_1_out), .D(and_5_out), .Q(LC_q), .reset(and_3_out));  // open: Qn, preset, en
  and and_5 (and_5_out, or_1_out, LA_qn);
  D_Flip_Flop RC (.clk(clock_1_out), .D(and_6_out), .Q(RC_q), .reset(and_4_out));  // open: Qn, preset, en
  and and_6 (and_6_out, or_2_out, RA_qn);
  or or_3 (or_3_out, LC_q, HAZARD);
  or or_4 (or_4_out, RC_q, HAZARD);
  D_Flip_Flop LB (.clk(clock_1_out), .D(and_7_out), .Q(LB_q), .reset(and_3_out));  // open: Qn, preset, en
  and and_7 (and_7_out, or_3_out, LA_qn);
  D_Flip_Flop RB (.clk(clock_1_out), .D(and_8_out), .Q(RB_q), .reset(and_4_out));  // open: Qn, preset, en
  and and_8 (and_8_out, or_4_out, RA_qn);
  or or_5 (or_5_out, LB_q, HAZARD);
  or or_6 (or_6_out, RB_q, HAZARD);
  D_Flip_Flop LA (.clk(clock_1_out), .D(and_9_out), .Qn(LA_qn), .reset(and_3_out));  // open: Q, preset, en
  and and_9 (and_9_out, or_5_out, LA_qn);
  D_Flip_Flop RA (.clk(clock_1_out), .D(and_10_out), .Qn(RA_qn), .reset(and_4_out));  // open: Q, preset, en
  and and_10 (and_10_out, or_6_out, RA_qn);
endmodule
