// Logisim project 9.1.1 D Flip Flops.circ as structural Verilog: 1 circuit, main circuit main
module main (
);

  wire and_1_out, and_2_out, and_3_out, and_4_out, and_5_out, and_6_out, and_7_out, clock_1_out, or_1_out,
       or_2_out, or_3_out, S0_q, S0_qn, S1_q, S1_qn, S2_q, S2_qn, S3_q, S3_qn;

  Clock clock_1 (.out(clock_1_out));
  D_Flip_Flop S3 (.clk(clock_1_out), .D(and_1_out), .Q(S3_q), .Qn(S3_qn));  // open: preset, en, reset
  and and_1 (and_1_out, S1_q, S0_qn);
  and and_2 (and_2_out, S3_qn, S2_qn, S1_q, S0_q);
  and and_3 (and_3_out, S3_q, S2_qn, S1_q, S0_qn);
  D_Flip_Flop S2 (.clk(clock_1_out), .D(or_1_out), .Q(S2_q), .Qn(S2_qn));  // open: preset, en, reset
  or or_1 (or_1_out, and_2_out, and_3_out);
  and and_4 (and_4_out, S1_q, S0_qn);
  or or_2 (or_2_out, and_4_out, and_5_out);
  and and_5 (and_5_out, S3_qn, S2_qn, S0_q);
  D_Flip_Flop S1 (.clk(clock_1_out), .D(or_2_out), .Q(S1_q), .Qn(S1_qn));  // open: preset, en, reset
  and and_6 (and_6_out, S3_qn, S2_qn, S1_qn);
  and and_7 (and_7_out, S3_q, S2_qn, S1_q, S0_qn);
  or or_3 (or_3_out, and_6_out, and_7_out);
  D_Flip_Flop S0 (.clk(clock_1_out), .D(or_3_out), .Q(S0_q), .Qn(S0_qn));  // open: preset, en, reset
endmodule
