// Logisim project 9.1.1JK.circ as structural Verilog: 1 circuit, main circuit main
module main (
);

  wire and_1_out, and_2_out, and_3_out, and_4_out, and_5_out, and_6_out, and_7_out, and_8_out, and_9_out,
       and_10_out, and_11_out, and_12_out, clock_1_out, or_1_out, or_2_out, or_3_out, or_4_out, S0_q, S0_qn,
       S1_q, S1_qn, S2_q, S2_qn, S3_q, S3_qn;

  Clock clock_1 (.out(clock_1_out));
  and and_1 (and_1_out, S3_qn, S2_q, S1_q, S0_qn);
  and and_2 (and_2_out, S3_q, S2_q, S1_q, S0_q);
  and and_3 (and_3_out, S3_qn, S2_qn, S1_q, S0_q);
  and and_4 (and_4_out, S3_q, S2_qn, S1_q, S0_qn);
  and and_5 (and_5_out, S3_qn, S2_q, S1_q, S0_qn);
  and and_6 (and_6_out, S3_q, S2_q, S1_q, S0_q);
  and and_7 (and_7_out, S3_qn, S2_qn, S1_qn, S0_q);
  and and_8 (and_8_out, S3_q, S2_q, S1_q, S0_q);
  and and_9 (and_9_out, S3_qn, S2_qn, S1_qn, S0_qn);
  and and_10 (and_10_out, S3_q, S2_qn, S1_q, S0_qn);
  and and_11 (and_11_out, S3_qn, S2_qn, S1_q, S0_q);
  and and_12 (and_12_out, S3_q, S2_q, S1_q, S0_q);
  or or_1 (or_1_out, and_9_out, and_10_out);
  or or_2 (or_2_out, and_11_out, and_12_out);
  or or_3 (or_3_out, and_3_out, and_4_out);
  or or_4 (or_4_out, and_5_out, and_6_out);
  J_K_Flip_Flop S3 (.J(and_1_out), .clk(clock_1_out), .K(and_2_out), .Q(S3_q), .Qn(S3_qn));  // open: preset, en, reset
  J_K_Flip_Flop S2 (.J(or_3_out), .clk(clock_1_out), .K(or_4_out), .Q(S2_q), .Qn(S2_qn));  // open: preset, en, reset
  J_K_Flip_Flop S1 (.J(and_7_out), .clk(clock_1_out), .K(and_8_out), .Q(S1_q), .Qn(S1_qn));  // open: preset, en, reset
  J_K_Flip_Flop S0 (.J(or_1_out), .clk(clock_1_out), .K(or_2_out), .Q(S0_q), .Qn(S0_qn));  // open: preset, en, reset
endmodule
