// Logisim project 9.1.1SR.circ as structural Verilog: 1 circuit, main circuit main
module main (
);

  wire and_1_out, and_2_out, and_3_out, and_4_out, and_5_out, and_6_out, and_7_out, and_8_out, and_9_out,
       and_10_out, and_11_out, and_12_out, and_13_out, and_14_out, and_15_out, and_16_out, and_17_out,
       clock_1_out, or_1_out, or_2_out, or_3_out, or_4_out, or_5_out, or_6_out, s_r_ff_1_q, s_r_ff_1_qn,
       s_r_ff_2_q, s_r_ff_2_qn, s_r_ff_3_q, s_r_ff_3_qn, s_r_ff_4_q, s_r_ff_4_qn;

  and and_1 (and_1_out, s_r_ff_1_qn, s_r_ff_2_q, s_r_ff_3_q, s_r_ff_4_qn);
  and and_2 (and_2_out, s_r_ff_1_q, s_r_ff_2_qn, s_r_ff_3_q, s_r_ff_4_qn);
  and and_3 (and_3_out, s_r_ff_1_q, s_r_ff_2_q, s_r_ff_3_q, s_r_ff_4_q);
  and and_4 (and_4_out, s_r_ff_1_qn, s_r_ff_2_qn, s_r_ff_3_q, s_r_ff_4_q);
  and and_5 (and_5_out, s_r_ff_1_q, s_r_ff_2_qn, s_r_ff_3_q, s_r_ff_4_qn);
  and and_6 (and_6_out, s_r_ff_1_q, s_r_ff_2_q, s_r_ff_3_q, s_r_ff_4_q);
  and and_7 (and_7_out, s_r_ff_1_qn, s_r_ff_2_q, s_r_ff_3_q, s_r_ff_4_qn);
  and and_8 (and_8_out, s_r_ff_1_qn, s_r_ff_2_qn, s_r_ff_3_qn, s_r_ff_4_q);
  and and_9 (and_9_out, s_r_ff_1_qn, s_r_ff_2_qn, s_r_ff_3_q, s_r_ff_4_q);
  and and_10 (and_10_out, s_r_ff_1_qn, s_r_ff_2_q, s_r_ff_3_q, s_r_ff_4_qn);
  and and_11 (and_11_out, s_r_ff_1_q, s_r_ff_2_qn, s_r_ff_3_q, s_r_ff_4_qn);
  and and_12 (and_12_out, s_r_ff_1_q, s_r_ff_2_q, s_r_ff_3_q, s_r_ff_4_q);
  and and_13 (and_13_out, s_r_ff_1_qn, s_r_ff_2_qn, s_r_ff_3_qn, s_r_ff_4_qn);
  and and_14 (and_14_out, s_r_ff_1_qn, s_r_ff_2_qn, s_r_ff_3_qn, s_r_ff_4_q);
  and and_15 (and_15_out, s_r_ff_1_q, s_r_ff_2_qn, s_r_ff_3_q, s_r_ff_4_qn);
  and and_16 (and_16_out, s_r_ff_1_q, s_r_ff_2_q, s_r_ff_3_q, s_r_ff_4_q);
  and and_17 (and_17_out, s_r_ff_1_qn, s_r_ff_2_qn, s_r_ff_3_q, s_r_ff_4_q);
  or or_1 (or_1_out, and_1_out, and_2_out);
  or or_2 (or_2_out, and_4_out, and_5_out);
  or or_3 (or_3_out, and_16_out, and_17_out);
  or or_4 (or_4_out, and_6_out, and_7_out);
  or or_5 (or_5_out, and_8_out, and_9_out, and_10_out, and_11_out);
  or or_6 (or_6_out, and_13_out, and_14_out, and_15_out);
  Clock clock_1 (.out(clock_1_out));
  S_R_Flip_Flop s_r_ff_1 (
    .S(or_1_out), .clk(clock_1_out), .R(and_3_out), .Q(s_r_ff_1_q), .Qn(s_r_ff_1_qn));  // open: preset, reset, en
  S_R_Flip_Flop s_r_ff_2 (
    .S(or_2_out), .clk(clock_1_out), .R(or_4_out), .Q(s_r_ff_2_q), .Qn(s_r_ff_2_qn));  // open: preset, reset, en
  S_R_Flip_Flop s_r_ff_3 (
    .S(or_5_out), .clk(clock_1_out), .R(and_12_out), .Q(s_r_ff_3_q), .Qn(s_r_ff_3_qn));  // open: preset, reset, en
  S_R_Flip_Flop s_r_ff_4 (
    .S(or_6_out), .clk(clock_1_out), .R(or_3_out), .Q(s_r_ff_4_q), .Qn(s_r_ff_4_qn));  // open: preset, reset, en
endmodule
