// Logisim project 9.1.1T.circ as structural Verilog: 1 circuit, main circuit main
module main (
);

  wire and_1_out, and_2_out, and_3_out, and_4_out, and_5_out, and_6_out, and_7_out, and_8_out, and_9_out,
       and_10_out, and_11_out, and_12_out, clock_1_out, or_1_out, or_2_out, or_3_out, or_4_out, t_ff_1_q,
       t_ff_1_qn, t_ff_2_q, t_ff_2_qn, t_ff_3_q, t_ff_3_qn, t_ff_4_q, t_ff_4_qn;

  and and_1 (and_1_out, t_ff_1_qn, t_ff_2_q, t_ff_3_q, t_ff_4_qn);
  and and_2 (and_2_out, t_ff_1_q, t_ff_2_q, t_ff_3_q, t_ff_4_q);
  and and_3 (and_3_out, t_ff_1_qn, t_ff_2_qn, t_ff_3_q, t_ff_4_q);
  and and_4 (and_4_out, t_ff_1_qn, t_ff_2_q, t_ff_3_q, t_ff_4_qn);
  and and_5 (and_5_out, t_ff_1_q, t_ff_2_qn, t_ff_3_q, t_ff_4_qn);
  and and_6 (and_6_out, t_ff_1_q, t_ff_2_q, t_ff_3_q, t_ff_4_q);
  and and_7 (and_7_out, t_ff_1_qn, t_ff_2_qn, t_ff_3_qn, t_ff_4_q);
  or or_1 (or_1_out, and_7_out, and_8_out);
  and and_8 (and_8_out, t_ff_1_q, t_ff_2_q, t_ff_3_q, t_ff_4_q);
  and and_9 (and_9_out, t_ff_1_qn, t_ff_2_qn, t_ff_3_qn, t_ff_4_qn);
  and and_10 (and_10_out, t_ff_1_qn, t_ff_2_qn, t_ff_3_q, t_ff_4_q);
  or or_2 (or_2_out, and_9_out, and_10_out, and_11_out, and_12_out);
  and and_11 (and_11_out, t_ff_1_q, t_ff_2_qn, t_ff_3_q, t_ff_4_qn);
  and and_12 (and_12_out, t_ff_1_q, t_ff_2_q, t_ff_3_q, t_ff_4_q);
  or or_3 (or_3_out, and_1_out, and_2_out);
  or or_4 (or_4_out, and_3_out, and_4_out, and_5_out, and_6_out);
  Clock clock_1 (.out(clock_1_out));
  T_Flip_Flop t_ff_1 (.clk(clock_1_out), .T(or_3_out), .Q(t_ff_1_q), .Qn(t_ff_1_qn));  // open: preset, reset, en
  T_Flip_Flop t_ff_2 (.clk(clock_1_out), .T(or_4_out), .Q(t_ff_2_q), .Qn(t_ff_2_qn));  // open: preset, reset, en
  T_Flip_Flop t_ff_3 (.clk(clock_1_out), .T(or_1_out), .Q(t_ff_3_q), .Qn(t_ff_3_qn));  // open: preset, reset, en
  T_Flip_Flop t_ff_4 (.clk(clock_1_out), .T(or_2_out), .Q(t_ff_4_q), .Qn(t_ff_4_qn));  // open: preset, reset, en
endmodule
