// Logisim project 9.2.1.circ as structural Verilog: 1 circuit, main circuit main
module main (
  input  [31:0] Input,
  input  Shift,
  output [31:0] Output
);

  wire and_1_out, clock_1_out, main_1_output, main_1_stall, main_2_output, main_2_stall, not_1_out,
       not_2_out, or_1_out, Original_bits_out;

  Clock clock_1 (.out(clock_1_out));
  and and_1 (and_1_out, Shift, ~or_1_out);  // AND_Gate
  Shift_Register #(.length(32)) Original_bits (
    .shift(and_1_out), .clk(clock_1_out), .out(Original_bits_out), .load(not_1_out), .d0(Input[31]),
    .d1(Input[30]), .d2(Input[29]), .d3(Input[28]), .d4(Input[27]), .d5(Input[26]), .d6(Input[25]),
    .d7(Input[24]), .d8(Input[23]), .d9(Input[22]), .d10(Input[21]), .d11(Input[20]), .d12(Input[19]),
    .d13(Input[18]), .d14(Input[17]), .d15(Input[16]), .d16(Input[15]), .d17(Input[14]), .d18(Input[13]),
    .d19(Input[12]), .d20(Input[11]), .d21(Input[10]), .d22(Input[9]), .d23(Input[8]), .d24(Input[7]),
    .d25(Input[6]), .d26(Input[5]), .d27(Input[4]), .d28(Input[3]), .d29(Input[2]), .d30(Input[1]),
    .d31(Input[0]));  // open: in, clr, q0, q1, q2, q3, q4, q5, q6, q7, q8, q9, q10, q11, q12, q13, q14, q15, q16, q17, q18, q19, q20, q21, q22, q23, q24, q25, q26, q27, q28, q29, q30, q31
  not not_1 (not_1_out, Shift);
  or or_1 (or_1_out, main_2_stall, main_1_stall);
  BitStuffer_main main_1 (.Input(Original_bits_out), .Stall(main_1_stall), .Clock(clock_1_out), .Output(main_1_output));
  Shift_Register #(.length(32)) View_of_Bits_being_stuffed (
    .shift(Shift), .in(main_1_output), .clk(clock_1_out));  // open: out, load, clr, d0, q0, d1, q1, d2, q2, d3, q3, d4, q4, d5, q5, d6, q6, d7, q7, d8, q8, d9, q9, d10, q10, d11, q11, d12, q12, d13, q13, d14, q14, d15, q15, d16, q16, d17, q17, d18, q18, d19, q19, d20, q20, d21, q21, d22, q22, d23, q23, d24, q24, d25, q25, d26, q26, d27, q27, d28, q28, d29, q29, d30, q30, d31, q31
  not not_2 (not_2_out, main_2_stall);
  Shift_Register #(.length(32)) Bits_Unstuffed (
    .shift(not_2_out), .in(main_2_output), .clk(clock_1_out), .q0(Output[31]), .q1(Output[30]),
    .q2(Output[29]), .q3(Output[28]), .q4(Output[27]), .q5(Output[26]), .q6(Output[25]), .q7(Output[24]),
    .q8(Output[23]), .q9(Output[22]), .q10(Output[21]), .q11(Output[20]), .q12(Output[19]), .q13(Output[18]),
    .q14(Output[17]), .q15(Output[16]), .q16(Output[15]), .q17(Output[14]), .q18(Output[13]),
    .q19(Output[12]), .q20(Output[11]), .q21(Output[10]), .q22(Output[9]), .q23(Output[8]), .q24(Output[7]),
    .q25(Output[6]), .q26(Output[5]), .q27(Output[4]), .q28(Output[3]), .q29(Output[2]), .q30(Output[1]),
    .q31(Output[0]));  // open: out, load, clr, d0, d1, d2, d3, d4, d5, d6, d7, d8, d9, d10, d11, d12, d13, d14, d15, d16, d17, d18, d19, d20, d21, d22, d23, d24, d25, d26, d27, d28, d29, d30, d31
  BitUnStuffer_main main_2 (.Input(main_1_output), .Stall(main_2_stall), .Clock(clock_1_out), .Output(main_2_output));
endmodule
