// Logisim project 9.2.2.circ as structural Verilog: 3 circuits, main circuit main
module main (
  input  [3:0] Multipilcand,
  input  [3:0] Multiplier,
  input  GO,
  input  RST,
  output DONE,
  output [7:0] product
);

  wire adder_1_cout, and_1_out, B_out, C_out, clock_1_out, control_thing_1_initial_load,
       control_thing_1_load_2, control_thing_1_shift_2, counter_1_carry;
  wire [3:0] adder_1_out, MCAND_q;

  Clock clock_1 (.out(clock_1_out));
  Control_Thing control_thing_1 (
    .Go(GO), .Clock(clock_1_out), .RST(RST), .Initial_Load(control_thing_1_initial_load),
    .Load_2(control_thing_1_load_2), .Shift_2(control_thing_1_shift_2), .Halt(DONE), .Load(product[0]),
    .Shift(counter_1_carry));
  Counter #(.width(3), .max('h6)) counter_1 (
    .load(clock_1_out), .D(3'b110), .carry(counter_1_carry), .clk(clock_1_out));  // open: count, Q, clr
  and and_1 (and_1_out, product[0], control_thing_1_load_2);
  Shift_Register #(.length(1)) C (
    .shift(control_thing_1_shift_2), .in(1'b0), .clk(clock_1_out), .out(C_out), .load(and_1_out),
    .clr(control_thing_1_initial_load), .d0(adder_1_cout));  // open: q0
  Register #(.width(4)) MCAND (
    .D(Multipilcand), .en(control_thing_1_initial_load), .Q(MCAND_q), .clk(clock_1_out));  // open: clr
  Shift_Register #(.length(4)) B (
    .shift(control_thing_1_shift_2), .in(C_out), .clk(clock_1_out), .out(B_out), .load(and_1_out),
    .clr(control_thing_1_initial_load), .d0(adder_1_out[3]), .q0(product[7]), .d1(adder_1_out[2]),
    .q1(product[6]), .d2(adder_1_out[1]), .q2(product[5]), .d3(adder_1_out[0]), .q3(product[4]));
  Adder #(.width(4)) adder_1 (.a(MCAND_q), .b(product[7:4]), .out(adder_1_out), .cout(adder_1_cout));  // open: cin
  Shift_Register #(.length(4)) Q (
    .shift(control_thing_1_shift_2), .in(B_out), .clk(clock_1_out), .load(control_thing_1_initial_load),
    .d0(Multiplier[3]), .q0(product[3]), .d1(Multiplier[2]), .q1(product[2]), .d2(Multiplier[1]),
    .q2(product[1]), .d3(Multiplier[0]), .q3(product[0]));  // open: out, clr
  // Probe on product
endmodule

module Control_Circuit (
  input  GO,
  input  ST,
  input  CLK,
  input  RST,
  output ILD,
  output LD,
  output HLT,
  output SH
);


  assign HLT = CLK;
  assign ILD = GO;
  assign LD = ST;
  assign SH = RST;
endmodule

module Control_Thing (
  input  Go,
  input  Shift,
  input  Load,
  input  Clock,
  input  RST,
  output Initial_Load,
  output Load_2,
  output Shift_2,
  output Halt
);

  wire and_1_out, d_ff_1_q, not_1_out;

  not not_1 (not_1_out, Shift);
  and and_1 (and_1_out, ~Go, Clock);  // AND_Gate
  and and_2 (Load_2, ~Go, not_1_out);  // AND_Gate
  D_Flip_Flop #(.trigger("falling")) d_ff_1 (
    .clk(and_1_out), .D(Load), .Q(d_ff_1_q), .reset(RST));  // open: Qn, preset, en
  or or_1 (Shift_2, d_ff_1_q, Load_2);

  assign Halt = Shift;
  assign Initial_Load = Go;
endmodule
