// Logisim project BitStuffer.circ as structural Verilog: 1 circuit, main circuit main
module main (
  input  Input,
  input  Clock,
  output Stall,
  output Output
);

  wire and_1_out, and_2_out, and_3_out, and_4_out, and_5_out, and_6_out, and_7_out, and_10_out, and_11_out,
       and_12_out, and_13_out, and_14_out, d_ff_1_q, d_ff_1_qn, d_ff_2_q, d_ff_2_qn, d_ff_3_q, d_ff_3_qn,
       not_1_out, or_1_out, or_2_out, or_3_out, or_4_out;

  and and_1 (and_1_out, d_ff_1_qn, d_ff_2_q, d_ff_3_q);
  and and_2 (and_2_out, d_ff_1_q, d_ff_2_qn, d_ff_3_qn);
  and and_3 (and_3_out, d_ff_1_qn, d_ff_2_q, d_ff_3_qn);
  and and_4 (and_4_out, d_ff_1_qn, d_ff_2_qn, d_ff_3_q);
  and and_5 (and_5_out, d_ff_1_q, d_ff_2_qn, d_ff_3_qn);
  and and_6 (and_6_out, d_ff_1_qn, d_ff_2_q, d_ff_3_qn);
  and and_7 (and_7_out, d_ff_1_qn, d_ff_2_qn, d_ff_3_qn);
  or or_1 (or_1_out, and_1_out, and_2_out);
  or or_2 (or_2_out, and_3_out, and_4_out);
  or or_3 (or_3_out, and_5_out, and_6_out, and_7_out);
  and and_8 (Stall, d_ff_1_q, d_ff_2_qn, d_ff_3_q);
  not not_1 (not_1_out, Input);
  D_Flip_Flop d_ff_1 (.clk(Clock), .D(or_1_out), .Q(d_ff_1_q), .Qn(d_ff_1_qn), .reset(not_1_out));  // open: preset, en
  D_Flip_Flop d_ff_2 (.clk(Clock), .D(or_2_out), .Q(d_ff_2_q), .Qn(d_ff_2_qn), .reset(not_1_out));  // open: preset, en
  D_Flip_Flop d_ff_3 (.clk(Clock), .D(or_3_out), .Q(d_ff_3_q), .Qn(d_ff_3_qn), .reset(not_1_out));  // open: preset, en
  and and_9 (Output, Input, or_4_out);
  and and_10 (and_10_out, d_ff_3_qn, d_ff_2_qn, d_ff_1_qn);
  and and_11 (and_11_out, d_ff_3_q, d_ff_2_qn, d_ff_1_qn);
  and and_12 (and_12_out, d_ff_3_qn, d_ff_2_q, d_ff_1_qn);
  and and_13 (and_13_out, d_ff_3_q, d_ff_2_q, d_ff_1_qn);
  and and_14 (and_14_out, d_ff_3_qn, d_ff_2_qn, d_ff_1_q);
  or or_4 (or_4_out, and_10_out, and_11_out, and_12_out, and_13_out, and_14_out);
endmodule
