// Logisim project MultiplierFramework.circ as structural Verilog: 2 circuits, main circuit Control
module Control (
  input  GO,
  input  ST,
  input  CLK,
  input  RST,
  output ILD,
  output LD,
  output HLT,
  output SH
);


  assign HLT = CLK;
  assign ILD = GO;
  assign LD = ST;
  assign SH = RST;
endmodule

module Multiplier (
  input  [3:0] Multipilcand,
  input  [3:0] Multiplier,
  input  GO,
  input  RST,
  output DONE,
  output [7:0] product
);

  wire adder_1_cout, and_1_out, B_out, C_out, clock_1_out, control_1_ild, control_1_ld, control_1_sh,
       counter_1_carry, or_1_out;
  wire [3:0] adder_1_out, MCAND_q;

  Clock clock_1 (.out(clock_1_out));
  Control control_1 (
    .ILD(control_1_ild), .LD(control_1_ld), .HLT(DONE), .SH(control_1_sh), .GO(GO), .ST(counter_1_carry),
    .CLK(clock_1_out), .RST(RST));
  or or_1 (or_1_out, control_1_ild, control_1_sh);
  Counter #(.width(3), .max('h7)) counter_1 (
    .load(or_1_out), .D(3'b011), .count(control_1_sh), .carry(counter_1_carry), .clk(clock_1_out));  // open: Q, clr
  and and_1 (and_1_out, product[0], control_1_ld);
  Shift_Register #(.length(1)) C (
    .shift(control_1_sh), .in(1'b0), .clk(clock_1_out), .out(C_out), .load(and_1_out), .clr(control_1_ild),
    .d0(adder_1_cout));  // open: q0
  Register #(.width(4)) MCAND (.D(Multipilcand), .en(control_1_ild), .Q(MCAND_q), .clk(clock_1_out));  // open: clr
  Shift_Register #(.length(4)) B (
    .shift(control_1_sh), .in(C_out), .clk(clock_1_out), .out(B_out), .load(and_1_out), .clr(control_1_ild),
    .d0(adder_1_out[3]), .q0(product[7]), .d1(adder_1_out[2]), .q1(product[6]), .d2(adder_1_out[1]),
    .q2(product[5]), .d3(adder_1_out[0]), .q3(product[4]));
  Adder #(.width(4)) adder_1 (.a(MCAND_q), .b(product[7:4]), .out(adder_1_out), .cout(adder_1_cout));  // open: cin
  Shift_Register #(.length(4)) Q (
    .shift(control_1_sh), .in(B_out), .clk(clock_1_out), .load(control_1_ild), .d0(Multiplier[3]),
    .q0(product[3]), .d1(Multiplier[2]), .q1(product[2]), .d2(Multiplier[1]), .q2(product[1]),
    .d3(Multiplier[0]), .q3(product[0]));  // open: out, clr
  // Probe on product
endmodule
