// Logisim project Coke machine.circ as structural Verilog: 4 circuits, main circuit main
module main (
  output [4:0] Quarters
);

  wire and_1_out, and_2_out, and_3_out, buffer_1_out, buffer_2_out, buffer_3_out, buffer_4_out, buffer_5_out,
       buffer_6_out, buffer_7_out, buffer_8_out, buffer_9_out, clock_1_out, Coin_Return_out, Coke_out,
       Collect_Change_out, comparator_1_load_counter, controlled_buffer_4_out, controlled_buffer_5_out,
       controlled_buffer_6_out, counter_1_carry, d_ff_1_q, d_ff_2_q, d_ff_3_qn, d_ff_4_q, d_ff_5_q, d_ff_6_q,
       Loonie_out, not_1_out, or_1_out, or_2_out, or_3_out, Pepsi_out, quarter_give_out_1_change,
       Quarter_out, Toonie_out;
  wire [2:0] controlled_buffer_1_out;
  wire [4:0] adder_1_out, comparator_1_out_2, multiplexer_1_out, quarter_give_out_1_quarters, ram_1_data,
       subtractor_1_out;

  Button Quarter (.out(Quarter_out));
  Button Loonie (.out(Loonie_out));
  Button Toonie (.out(Toonie_out));
  assign controlled_buffer_1_out[0] = not_1_out ? Quarter_out : 1'bz;  // Controlled_Buffer controlled_buffer_1
  assign controlled_buffer_1_out[1] = not_1_out ? Loonie_out : 1'bz;  // Controlled_Buffer controlled_buffer_2
  assign controlled_buffer_1_out[2] = not_1_out ? Toonie_out : 1'bz;  // Controlled_Buffer controlled_buffer_3
  not not_1 (not_1_out, comparator_1_load_counter);
  Button Coin_Return (.out(Coin_Return_out));
  LED Choose_Drink (.in(comparator_1_load_counter));
  Button Coke (.out(Coke_out));
  Button Pepsi (.out(Pepsi_out));
  Button Collect_Change (.out(Collect_Change_out));
  or or_1 (or_1_out, Coke_out, Pepsi_out);
  Multiplexer #(.select(3), .width(5), .enable("false")) multiplexer_1 (
    .in1(5'b00001), .in2(5'b00100), .in4(5'b01000), .out(multiplexer_1_out), .sel(controlled_buffer_1_out));  // open: in0, in3, in5, in6, in7
  Comparator comparator_1 (
    .in_1(ram_1_data), .out_2(comparator_1_out_2), .Load_Counter(comparator_1_load_counter));  // open: bottom_of_counter
  buf buffer_1 (buffer_1_out, buffer_2_out);
  buf buffer_2 (buffer_2_out, or_2_out);
  or or_2 (or_2_out, controlled_buffer_1_out[0], controlled_buffer_1_out[1], controlled_buffer_1_out[2]);
  D_Flip_Flop d_ff_1 (
    .clk(or_1_out), .D(comparator_1_load_counter), .Q(d_ff_1_q), .reset(Collect_Change_out));  // open: Qn, preset, en
  buf buffer_3 (buffer_3_out, buffer_5_out);
  buf buffer_4 (buffer_4_out, buffer_1_out);
  buf buffer_5 (buffer_5_out, buffer_6_out);
  buf buffer_6 (buffer_6_out, buffer_4_out);
  Subtractor #(.width(5)) subtractor_1 (
    .a(comparator_1_out_2), .b(5'b00111), .out(subtractor_1_out));  // open: bin, bout
  D_Flip_Flop #(.trigger("falling")) d_ff_2 (
    .clk(controlled_buffer_5_out), .D(d_ff_1_q), .Q(d_ff_2_q), .reset(Collect_Change_out));  // open: Qn, preset, en
  Adder #(.width(5)) adder_1 (.a(multiplexer_1_out), .b(ram_1_data), .out(adder_1_out));  // open: cin, cout
  buf buffer_7 (buffer_7_out, buffer_9_out);
  buf buffer_8 (buffer_8_out, buffer_3_out);
  buf buffer_9 (buffer_9_out, buffer_8_out);
  Counter #(.width(5), .max('h1f), .ongoal("load"), .trigger("falling")) counter_1 (
    .load(d_ff_1_q), .D(subtractor_1_out), .count(d_ff_2_q), .carry(counter_1_carry),
    .clk(controlled_buffer_4_out), .clr(Collect_Change_out));  // open: Q
  assign controlled_buffer_4_out = d_ff_1_q ? controlled_buffer_5_out : 1'bz;  // Controlled_Buffer controlled_buffer_4
  assign controlled_buffer_5_out = d_ff_3_qn ? clock_1_out : 1'bz;  // Controlled_Buffer controlled_buffer_5
  Clock clock_1 (.out(clock_1_out));
  assign controlled_buffer_6_out = and_1_out ? controlled_buffer_5_out : 1'bz;  // Controlled_Buffer controlled_buffer_6
  and and_1 (and_1_out, d_ff_1_q, d_ff_2_q);
  RAM #(.addrWidth(2), .dataWidth(5), .bus("separate")) ram_1 (
    .addr(2'b00), .din(adder_1_out), .data(ram_1_data), .clk(buffer_7_out), .clr(Collect_Change_out));  // open: str, sel, ld
  Quarter_Give_Out quarter_give_out_1 (
    .Reset_Change(d_ff_2_q), .Finished(counter_1_carry), .Add_quarters(d_ff_1_q),
    .Clock(controlled_buffer_6_out), .Reset(Collect_Change_out), .Change(quarter_give_out_1_change),
    .Quarters(quarter_give_out_1_quarters));
  and and_2 (and_2_out, Coke_out, d_ff_1_q);
  and and_3 (and_3_out, Pepsi_out, d_ff_1_q);
  D_Flip_Flop d_ff_3 (
    .clk(clock_1_out), .D(or_3_out), .Qn(d_ff_3_qn), .reset(Collect_Change_out));  // open: Q, preset, en
  D_Flip_Flop d_ff_4 (
    .clk(Coin_Return_out), .D(Coin_Return_out), .Q(d_ff_4_q), .reset(Collect_Change_out));  // open: Qn, preset, en
  or or_3 (or_3_out, d_ff_4_q, quarter_give_out_1_change);
  D_Flip_Flop d_ff_5 (
    .clk(and_2_out), .D(and_2_out), .Q(d_ff_5_q), .reset(Collect_Change_out));  // open: Qn, preset, en
  D_Flip_Flop d_ff_6 (
    .clk(and_3_out), .D(and_3_out), .Q(d_ff_6_q), .reset(Collect_Change_out));  // open: Qn, preset, en
  LED Change (.in(or_3_out));
  Multiplexer #(.width(5), .enable("false")) multiplexer_2 (
    .in0(quarter_give_out_1_quarters), .in1(ram_1_data), .out(Quarters), .sel(d_ff_4_q));
  LED Coke_2 (.in(d_ff_5_q));
  LED Pepsi_2 (.in(d_ff_6_q));
endmodule

module Comparator (
  input  [4:0] in_1,
  output [4:0] out_2,
  output Load_Counter,
  output bottom_of_counter
);

  wire and_1_out, and_2_out, and_3_out, and_4_out, and_5_out, and_6_out;

  and and_1 (and_1_out, ~in_1[0], ~in_1[1], ~in_1[2], ~in_1[3]);  // AND_Gate
  and and_2 (and_2_out, ~in_1[3], ~in_1[2], ~in_1[1], in_1[0]);  // AND_Gate
  and and_3 (and_3_out, ~in_1[0], in_1[1], ~in_1[2], ~in_1[3]);  // AND_Gate
  and and_4 (and_4_out, in_1[0], in_1[1], ~in_1[2], ~in_1[3]);  // AND_Gate
  and and_5 (and_5_out, ~in_1[0], ~in_1[1], in_1[2], ~in_1[3]);  // AND_Gate
  and and_6 (and_6_out, in_1[0], ~in_1[1], in_1[2], ~in_1[3]);  // AND_Gate
  and and_7 (Load_Counter, ~and_1_out, ~and_2_out, ~and_3_out, ~and_4_out, ~and_5_out, ~and_6_out);  // AND_Gate
  assign out_2 = Load_Counter ? in_1 : 5'bz;  // Controlled_Buffer controlled_buffer_1
  not not_1 (bottom_of_counter, Load_Counter);
endmodule

module Quarter_Give_Out (
  input  Reset_Change,
  input  Finished,
  input  Add_quarters,
  input  Clock,
  input  Reset,
  output Change,
  output [4:0] Quarters
);

  and and_1 (Change, Reset_Change, Finished);
  Counter #(.width(5), .max('h1f)) counter_1 (
    .count(Add_quarters), .Q(Quarters), .clk(Clock), .clr(Reset));  // open: load, D, carry
endmodule

module Reset_Comparator (
  input  [4:0] in_1,
  input  in_2,
  output out_3
);

  wire and_1_out;

  and and_1 (and_1_out, ~in_1[4], ~in_1[3], ~in_1[2], ~in_1[1], ~in_1[0]);  // AND_Gate
  and and_2 (out_3, and_1_out, in_2);
endmodule
