// Logisim project 6.4.1.circ as structural Verilog: 1 circuit, main circuit main
module main (
  input  D,
  input  C,
  output Q,
  output nQ
);

  wire nand_1_out, nand_2_out, nand_3_out, nand_4_out, nand_5_out, nand_6_out, not_1_out;

  nand nand_1 (nand_1_out, D, C);
  nand nand_2 (nand_2_out, C, ~D);  // NAND_Gate
  nand nand_3 (nand_3_out, nand_1_out, nand_4_out);
  nand nand_4 (nand_4_out, nand_3_out, nand_2_out);
  not not_1 (not_1_out, C);
  nand nand_5 (nand_5_out, nand_3_out, not_1_out);
  nand nand_6 (nand_6_out, not_1_out, ~nand_4_out);  // NAND_Gate
  nand nand_7 (Q, nand_5_out, nQ);
  nand nand_8 (nQ, Q, nand_6_out);
endmodule
