// Logisim project 6.4.2.2.circ as structural Verilog: 1 circuit, main circuit main
module main (
  input  DA,
  input  X,
  input  DB,
  input  C,
  output Y
);

  wire and_1_out, and_2_out, and_3_out, d_ff_1_q, d_ff_2_qn, or_1_out, or_2_out;

  and and_1 (and_1_out, DA, X);
  and and_2 (and_2_out, X, DB);
  or or_1 (or_1_out, and_1_out, and_2_out);
  and and_3 (and_3_out, ~DA, X);  // AND_Gate
  D_Flip_Flop d_ff_1 (.clk(C), .D(or_1_out), .Q(d_ff_1_q));  // open: Qn, preset, en, reset
  D_Flip_Flop d_ff_2 (.clk(C), .D(and_3_out), .Qn(d_ff_2_qn));  // open: Q, preset, en, reset
  or or_2 (or_2_out, d_ff_1_q, d_ff_2_qn);
  and and_4 (Y, or_2_out, ~X);  // AND_Gate
endmodule
