// Logisim project 6.4.2.circ as structural Verilog: 1 circuit, main circuit main
module main (
  input  DA,
  input  X,
  input  DB,
  input  C,
  output A,
  output nA,
  output Y,
  output B,
  output nB
);

  wire and_1_out, and_2_out, and_3_out, nand_1_out, nand_2_out, nand_3_out, nand_4_out, nand_5_out,
       nand_6_out, nand_7_out, nand_8_out, nand_9_out, nand_10_out, nand_11_out, nand_12_out, not_1_out,
       or_1_out, or_2_out;

  and and_1 (and_1_out, DA, X);
  and and_2 (and_2_out, X, DB);
  or or_1 (or_1_out, and_1_out, and_2_out);
  and and_3 (and_3_out, ~DA, X);  // AND_Gate
  nand nand_1 (nand_1_out, or_1_out, C);
  nand nand_2 (nand_2_out, C, ~or_1_out);  // NAND_Gate
  nand nand_3 (nand_3_out, and_3_out, C);
  nand nand_4 (nand_4_out, C, ~and_3_out);  // NAND_Gate
  nand nand_5 (nand_5_out, nand_1_out, nand_6_out);
  nand nand_6 (nand_6_out, nand_5_out, nand_2_out);
  nand nand_7 (nand_7_out, nand_3_out, nand_8_out);
  nand nand_8 (nand_8_out, nand_7_out, nand_4_out);
  nand nand_9 (nand_9_out, not_1_out, ~nand_8_out);  // NAND_Gate
  not not_1 (not_1_out, C);
  nand nand_10 (nand_10_out, nand_5_out, not_1_out);
  nand nand_11 (nand_11_out, not_1_out, ~nand_6_out);  // NAND_Gate
  nand nand_12 (nand_12_out, nand_7_out, not_1_out);
  nand nand_13 (A, nand_10_out, nA);
  nand nand_14 (nA, A, nand_11_out);
  nand nand_15 (B, nand_12_out, nB);
  nand nand_16 (nB, B, nand_9_out);
  or or_2 (or_2_out, A, B);
  and and_4 (Y, or_2_out, ~X);  // AND_Gate
endmodule
