// Logisim project 6.4.3.circ as structural Verilog: 1 circuit, main circuit main
module main (
  input  X
);

  wire and_1_out, and_2_out, and_3_out, and_4_out, d_ff_1_q, d_ff_2_q, or_1_out, or_2_out;

  and and_1 (and_1_out, d_ff_2_q, ~X);  // AND_Gate
  and and_2 (and_2_out, X, d_ff_1_q);
  and and_3 (and_3_out, ~d_ff_1_q, ~X);  // AND_Gate
  and and_4 (and_4_out, X, d_ff_2_q);
  or or_1 (or_1_out, and_1_out, and_2_out);
  or or_2 (or_2_out, and_3_out, and_4_out);
  D_Flip_Flop d_ff_1 (.clk(X), .D(or_1_out), .Q(d_ff_1_q));  // open: Qn, preset, en, reset
  D_Flip_Flop d_ff_2 (.clk(X), .D(or_2_out), .Q(d_ff_2_q));  // open: Qn, preset, en, reset

  // Notes on the sheet:
  //   DA
  //   DB
endmodule
