// Logisim project 6.4.4.circ as structural Verilog: 1 circuit, main circuit main
module main (
  input  X,
  output Y
);

  wire clock_1_out, not_1_out, s_r_ff_1_q, s_r_ff_2_q, s_r_ff_2_qn, xor_1_out;

  Clock clock_1 (.out(clock_1_out));
  S_R_Flip_Flop s_r_ff_1 (
    .S(s_r_ff_2_q), .clk(clock_1_out), .R(s_r_ff_2_qn), .Q(s_r_ff_1_q));  // open: Qn, preset, reset, en
  LED A (.in(s_r_ff_1_q));
  not not_1 (not_1_out, xor_1_out);
  xor xor_1 (xor_1_out, s_r_ff_1_q, X);
  S_R_Flip_Flop s_r_ff_2 (
    .S(not_1_out), .clk(clock_1_out), .R(xor_1_out), .Q(s_r_ff_2_q), .Qn(s_r_ff_2_qn));  // open: preset, reset, en
  LED B (.in(s_r_ff_2_q));
  xor xor_2 (Y, s_r_ff_2_q, xor_1_out);

  // Notes on the sheet:
  //   SA
  //   RA
  //   SB
  //   RB
endmodule
