// Logisim project 8 bit adder(modified)(sub2).circ as structural Verilog: 2 circuits, main circuit main
module main (
  input  A,
  input  B,
  input  Carry_in,
  output S1,
  output C
);

  wire and_1_out, and_2_out, xor_1_out;

  xor xor_1 (xor_1_out, A, B);
  and and_1 (and_1_out, A, B);
  xor xor_2 (S1, xor_1_out, Carry_in);
  or or_1 (C, and_1_out, and_2_out);
  and and_2 (and_2_out, xor_1_out, Carry_in);
endmodule

module _4_Bit_Adder (
  input  [7:0] in_1,
  input  [7:0] in_2,
  output [7:0] S
);

  wire main_1_c, main_2_c, main_3_c, main_4_c, main_5_c, main_6_c, main_7_c;

  main main_1 (.A(in_1[0]), .B(in_2[0]), .Carry_in(1'b0), .S1(S[0]), .C(main_1_c));
  main main_2 (.A(in_1[1]), .B(in_2[1]), .Carry_in(main_1_c), .S1(S[1]), .C(main_2_c));
  main main_3 (.A(in_1[2]), .B(in_2[2]), .Carry_in(main_2_c), .S1(S[2]), .C(main_3_c));
  main main_4 (.A(in_1[3]), .B(in_2[3]), .Carry_in(main_3_c), .S1(S[3]), .C(main_4_c));
  main main_5 (.A(in_2[4]), .B(in_1[4]), .Carry_in(main_4_c), .S1(S[4]), .C(main_5_c));
  main main_6 (.A(in_1[5]), .B(in_2[5]), .Carry_in(main_5_c), .S1(S[5]), .C(main_6_c));
  main main_7 (.A(in_1[6]), .B(in_2[6]), .Carry_in(main_6_c), .S1(S[6]), .C(main_7_c));
  main main_8 (.A(in_1[7]), .B(in_2[7]), .Carry_in(main_7_c), .S1(S[7]));  // open: C
endmodule
