// Logisim project Contraction.circ as structural Verilog: 1 circuit, main circuit main
module main (
  input  [7:0] in_1,
  input  [7:0] in_2,
  input  Add_or_Subtract,
  output [7:0] out_4
);

  wire [7:0] n4_bit_adder_1_s, n4_bit_adder_2_s;

  _4_Bit_Adder u_4_bit_adder_1 (.in_1(in_1), .S(n4_bit_adder_1_s));
  _4_Bit_Adder u_4_bit_adder_2 (.in_1(in_1), .in_2(in_2), .S(n4_bit_adder_2_s));
  Multiplexer #(.width(8), .enable("false")) multiplexer_1 (
    .in0(n4_bit_adder_1_s), .in1(n4_bit_adder_2_s), .out(out_4), .sel(Add_or_Subtract));
endmodule
